// Logisim project trabac.circ as structural Verilog: 6 circuits, main circuit main
module main (
  input  A0,
  input  A1,
  input  A2,
  input  A3,
  input  B0,
  input  B1,
  input  B2,
  input  B3,
  output S0,
  output out_10,
  output S1,
  output S2,
  output S3
);

  wire decodificador_1_a, decodificador_1_b, decodificador_1_c, decodificador_1_d, decodificador_1_e,
       decodificador_1_f, decodificador_1_g, decodificador_2_a, decodificador_2_b, decodificador_2_c,
       decodificador_2_d, decodificador_2_e, decodificador_2_f, decodificador_2_g, decodificador_3_a,
       decodificador_3_b, decodificador_3_c, decodificador_3_d, decodificador_3_e, decodificador_3_f,
       decodificador_3_g;

  somador_completo somador_completo_1 (
    .a0(A0), .b0(B0), .a1(A1), .b1(B1), .a2(A2), .b2(B2), .a3(A3), .b3(B3), .Overflow(out_10), .s0(S0),
    .s1(S1), .s2(S2), .s3(S3));
  decodificador decodificador_1 (
    .E0(A3), .E1(A2), .E2(A1), .E3(A0), .A(decodificador_1_a), .B(decodificador_1_b), .C(decodificador_1_c),
    .D(decodificador_1_d), .E(decodificador_1_e), .F(decodificador_1_f), .G(decodificador_1_g));
  decodificador decodificador_2 (
    .E0(B3), .E1(B2), .E2(B1), .E3(B0), .A(decodificador_2_a), .B(decodificador_2_b), .C(decodificador_2_c),
    .D(decodificador_2_d), .E(decodificador_2_e), .F(decodificador_2_f), .G(decodificador_2_g));
  _7_Segment_Display u_7_segment_display_1 (
    .g(decodificador_1_g), .f(decodificador_1_f), .a(decodificador_1_a), .b(decodificador_1_b),
    .e(decodificador_1_e), .d(decodificador_1_d), .c(decodificador_1_c));  // open: dp
  _7_Segment_Display u_7_segment_display_2 (
    .g(decodificador_2_g), .f(decodificador_2_f), .a(decodificador_2_a), .b(decodificador_2_b),
    .e(decodificador_2_e), .d(decodificador_2_d), .c(decodificador_2_c));  // open: dp
  decodificador decodificador_3 (
    .E0(S3), .E1(S2), .E2(S1), .E3(S0), .A(decodificador_3_a), .B(decodificador_3_b), .C(decodificador_3_c),
    .D(decodificador_3_d), .E(decodificador_3_e), .F(decodificador_3_f), .G(decodificador_3_g));
  _7_Segment_Display u_7_segment_display_3 (
    .g(decodificador_3_g), .f(decodificador_3_f), .a(decodificador_3_a), .b(decodificador_3_b),
    .e(decodificador_3_e), .d(decodificador_3_d), .c(decodificador_3_c));  // open: dp
endmodule

module decodificador (
  input  E0,
  input  E1,
  input  E2,
  input  E3,
  output A,
  output B,
  output C,
  output D,
  output E,
  output F,
  output G
);

  wire and_1_out, and_2_out, and_3_out, and_4_out, and_5_out, and_6_out, and_7_out, and_8_out, and_9_out,
       and_10_out, and_11_out, and_12_out, and_13_out, and_14_out, and_15_out, and_16_out, and_17_out,
       and_18_out, and_19_out, and_20_out, and_21_out, and_22_out, and_23_out, and_24_out, and_25_out,
       and_26_out, and_27_out, and_28_out, and_29_out, and_30_out, and_31_out, and_32_out, and_33_out,
       and_34_out, and_35_out, and_36_out, and_37_out, and_38_out, and_39_out, and_40_out, and_41_out,
       and_42_out, and_43_out, and_44_out, and_45_out, and_46_out, not_1_out, not_2_out, not_3_out,
       not_4_out, not_5_out, not_6_out, not_7_out, not_8_out, not_9_out, not_10_out, not_11_out, not_12_out,
       not_13_out, not_14_out, not_15_out, not_16_out, not_17_out, not_18_out, not_19_out, not_20_out,
       not_21_out, not_22_out, not_23_out, not_24_out, not_25_out, not_26_out, not_27_out, not_28_out,
       not_29_out, not_30_out, not_31_out, not_32_out, not_33_out, not_34_out, not_35_out, not_36_out,
       not_37_out, not_38_out, not_39_out, not_40_out, not_41_out, not_42_out, not_43_out, or_1_out,
       or_2_out, or_3_out, or_4_out, or_5_out, or_6_out, or_7_out, or_8_out, or_9_out, or_10_out, or_12_out,
       or_13_out, or_14_out, or_15_out, or_16_out, or_17_out, or_18_out, or_20_out, or_21_out, or_22_out,
       or_23_out;

  not not_1 (not_1_out, E1);
  not not_2 (not_2_out, E3);
  not not_3 (not_3_out, E0);
  not not_4 (not_4_out, E0);
  and and_1 (and_1_out, E0, not_5_out);
  not not_5 (not_5_out, E1);
  not not_6 (not_6_out, E2);
  not not_7 (not_7_out, E0);
  not not_8 (not_8_out, E1);
  not not_9 (not_9_out, E0);
  and and_2 (and_2_out, not_9_out, not_10_out);
  not not_10 (not_10_out, E2);
  not not_11 (not_11_out, E3);
  not not_12 (not_12_out, E0);
  not not_13 (not_13_out, E2);
  not not_14 (not_14_out, E0);
  and and_3 (and_3_out, not_14_out, not_15_out);
  not not_15 (not_15_out, E2);
  not not_16 (not_16_out, E0);
  and and_4 (and_4_out, not_16_out, E3);
  not not_17 (not_17_out, E2);
  not not_18 (not_18_out, E0);
  not not_19 (not_19_out, E1);
  not not_20 (not_20_out, E0);
  and and_5 (and_5_out, not_20_out, not_21_out);
  not not_21 (not_21_out, E1);
  not not_22 (not_22_out, E3);
  not not_23 (not_23_out, E1);
  and and_6 (and_6_out, not_23_out, E2);
  not not_24 (not_24_out, E2);
  not not_25 (not_25_out, E1);
  and and_7 (and_7_out, not_25_out, not_26_out);
  not not_26 (not_26_out, E3);
  and and_8 (and_8_out, E2, not_27_out);
  not not_27 (not_27_out, E3);
  and and_9 (and_9_out, E0, E2);
  and and_10 (and_10_out, E0, E1);
  not not_28 (not_28_out, E2);
  not not_29 (not_29_out, E3);
  not not_30 (not_30_out, E0);
  and and_11 (and_11_out, not_30_out, E1);
  not not_31 (not_31_out, E2);
  not not_32 (not_32_out, E1);
  and and_12 (and_12_out, not_32_out, E2);
  and and_13 (and_13_out, E2, not_33_out);
  not not_33 (not_33_out, E3);
  not not_34 (not_34_out, E0);
  and and_14 (and_14_out, not_34_out, E1);
  not not_35 (not_35_out, E2);
  not not_36 (not_36_out, E1);
  and and_15 (and_15_out, not_1_out, not_2_out);
  and and_16 (and_16_out, not_3_out, E2);
  and and_17 (and_17_out, not_4_out, E1);
  and and_18 (and_18_out, E1, E2);
  and and_19 (and_19_out, and_1_out, not_6_out);
  not not_37 (not_37_out, E3);
  and and_20 (and_20_out, not_7_out, not_8_out);
  and and_21 (and_21_out, and_2_out, not_11_out);
  not not_38 (not_38_out, E1);
  not not_39 (not_39_out, E3);
  and and_22 (and_22_out, not_12_out, E2);
  and and_23 (and_23_out, E0, not_13_out);
  or or_1 (or_1_out, and_3_out, and_4_out);
  and and_24 (and_24_out, not_17_out, E3);
  and and_25 (and_25_out, not_18_out, E1);
  and and_26 (and_26_out, E0, not_19_out);
  and and_27 (and_27_out, and_5_out, not_22_out);
  and and_28 (and_28_out, and_6_out, E3);
  and and_29 (and_29_out, E1, not_24_out);
  and and_30 (and_30_out, E1, E2);
  not not_40 (not_40_out, E3);
  not not_41 (not_41_out, E2);
  or or_2 (or_2_out, and_7_out, and_8_out);
  or or_3 (or_3_out, and_9_out, and_10_out);
  and and_31 (and_31_out, not_28_out, not_29_out);
  and and_32 (and_32_out, and_11_out, not_31_out);
  not not_42 (not_42_out, E3);
  not not_43 (not_43_out, E1);
  or or_4 (or_4_out, and_12_out, and_13_out);
  and and_33 (and_33_out, and_14_out, not_35_out);
  and and_34 (and_34_out, E0, not_36_out);
  and and_35 (and_35_out, E0, E3);
  or or_5 (or_5_out, and_15_out, and_16_out);
  and and_36 (and_36_out, and_17_out, E3);
  or or_6 (or_6_out, and_18_out, and_19_out);
  and and_37 (and_37_out, E0, not_37_out);
  or or_7 (or_7_out, and_20_out, and_21_out);
  and and_38 (and_38_out, not_38_out, not_39_out);
  and and_39 (and_39_out, and_22_out, E3);
  and and_40 (and_40_out, and_23_out, E3);
  or or_8 (or_8_out, or_1_out, and_24_out);
  or or_9 (or_9_out, and_25_out, and_26_out);
  or or_10 (or_10_out, and_27_out, and_28_out);
  and and_41 (and_41_out, and_29_out, E3);
  and and_42 (and_42_out, and_30_out, not_40_out);
  and and_43 (and_43_out, E0, not_41_out);
  or or_11 (E, or_2_out, or_3_out);
  or or_12 (or_12_out, and_31_out, and_32_out);
  and and_44 (and_44_out, E1, not_42_out);
  and and_45 (and_45_out, E0, not_43_out);
  and and_46 (and_46_out, E0, E2);
  or or_13 (or_13_out, or_4_out, and_33_out);
  or or_14 (or_14_out, and_34_out, and_35_out);
  or or_15 (or_15_out, or_5_out, and_36_out);
  or or_16 (or_16_out, or_6_out, and_37_out);
  or or_17 (or_17_out, or_7_out, and_38_out);
  or or_18 (or_18_out, and_39_out, and_40_out);
  or or_19 (C, or_8_out, or_9_out);
  or or_20 (or_20_out, or_10_out, and_41_out);
  or or_21 (or_21_out, and_42_out, and_43_out);
  or or_22 (or_22_out, or_12_out, and_44_out);
  or or_23 (or_23_out, and_45_out, and_46_out);
  or or_24 (G, or_13_out, or_14_out);
  or or_25 (A, or_15_out, or_16_out);
  or or_26 (B, or_17_out, or_18_out);
  or or_27 (D, or_20_out, or_21_out);
  or or_28 (F, or_22_out, or_23_out);
endmodule

module soma_1 (
  input  a,
  input  b,
  output soma,
  output co
);

  and and_1 (co, b, a);
  xor xor_1 (soma, a, b);
endmodule

module somador_1_bit (
  input  ci,
  input  a,
  input  b,
  output S,
  output co
);

  wire soma1_2_1_co, soma1_2_1_s, soma1_2_2_co;

  soma1_2 soma1_2_1 (.in_1(a), .in_2(b), .Co(soma1_2_1_co), .S(soma1_2_1_s));
  soma1_2 soma1_2_2 (.in_1(ci), .in_2(soma1_2_1_s), .Co(soma1_2_2_co), .S(S));
  or u_co (co, soma1_2_1_co, soma1_2_2_co);
endmodule

module somador_completo (
  input  a0,
  input  b0,
  input  a1,
  input  b1,
  input  a2,
  input  b2,
  input  a3,
  input  b3,
  output s0,
  output s1,
  output s2,
  output s3,
  output Overflow
);

  wire somador_1_bit_1_co, somador_1_bit_2_co, somador_1_bit_3_co;

  somador_1_bit somador_1_bit_1 (.ci(1'b0), .a(a0), .b(b0), .co(somador_1_bit_1_co), .S(s0));
  somador_1_bit somador_1_bit_2 (.ci(somador_1_bit_1_co), .a(a1), .b(b1), .co(somador_1_bit_2_co), .S(s1));
  somador_1_bit somador_1_bit_3 (.ci(somador_1_bit_2_co), .a(a2), .b(b2), .co(somador_1_bit_3_co), .S(s2));
  somador_1_bit somador_1_bit_4 (.ci(somador_1_bit_3_co), .a(a3), .b(b3), .co(Overflow), .S(s3));
endmodule

module soma1_2 (
  input  in_1,
  input  in_2,
  output S,
  output Co
);

  and and_1 (Co, in_2, in_1);
  xor xor_1 (S, in_1, in_2);
endmodule
