// Logisim project trabac02.circ as structural Verilog
module ULA (
  input  a,
  input  b,
  input  Cin,
  input  [2:0] \Bit_de_seleção ,
  output \Saída ,
  output Co
);

  wire and_1_out, multiplexer_1_out, not_1_out, not_2_out, or_1_out, soma_1_soma;

  not not_1 (not_1_out, b);
  and and_1 (and_1_out, a, multiplexer_1_out);
  Multiplexer #(.select(3), .enable("false")) multiplexer_1 (
    .in0(b), .in1(b), .in2(b), .in3(b), .in4(not_1_out), .in5(b), .in6(b), .in7(b), .out(multiplexer_1_out),
    .sel(\Bit_de_seleção ));
  or or_1 (or_1_out, a, multiplexer_1_out);
  not not_2 (not_2_out, a);
  soma soma_1 (.Cin(Cin), .a(a), .b(multiplexer_1_out), .soma(soma_1_soma), .co(Co));
  Multiplexer #(.select(3), .enable("false")) multiplexer_2 (
    .in0(and_1_out), .in1(or_1_out), .in2(not_2_out), .in3(soma_1_soma), .in4(soma_1_soma), .out(\Saída ),
    .sel(\Bit_de_seleção ));  // open: in5, in6, in7

  // Notes on the sheet:
  //   Adicionando o B invertido
  //   Caso contrário, será B normal
  //   Foi adicionado
  //   um terceiro bit 
  //   para que a subtração
  //   tenha o OP Code 100
  //   apenas sairá B invertido se o bit de seleção for 100
endmodule

module soma (
  input  Cin,
  input  a,
  input  b,
  output soma,
  output co
);

  wire xor_1_out;

  xor xor_1 (xor_1_out, a, b);
  and and_1 (co, a, b);
  xor xor_2 (soma, Cin, xor_1_out);
endmodule

module ULA_4bit (
  input  [2:0] \Bits_de_seleção ,
  input  B3,
  input  B2,
  input  B1,
  input  B0,
  input  A3,
  input  A2,
  input  A1,
  input  A0,
  input  Cin,
  output S0,
  output S1,
  output S2,
  output S3,
  output Co
);

  wire ula0_co, ula1_co, ula2_co;

  ULA ula0 (.a(A0), .b(B0), .Cin(Cin), .\Bit_de_seleção (\Bits_de_seleção ), .\Saída (S0), .Co(ula0_co));
  ULA ula1 (.a(A1), .b(B1), .Cin(ula0_co), .\Bit_de_seleção (\Bits_de_seleção ), .\Saída (S1), .Co(ula1_co));
  ULA ula2 (.a(A2), .b(B2), .Cin(ula1_co), .\Bit_de_seleção (\Bits_de_seleção ), .\Saída (S2), .Co(ula2_co));
  ULA ula3 (.a(A3), .b(B3), .Cin(ula2_co), .\Bit_de_seleção (\Bits_de_seleção ), .\Saída (S3), .Co(Co));
endmodule

module ULAtotal (
  input  [3:0] A,
  input  [3:0] B,
  input  [3:0] \Bits_de_seleção ,
  output [3:0] \Saída 
);

  wire [3:0] and_1_out, and_2_out, and_3_out, and_4_out, not_1_out, not_2_out, not_3_out, not_4_out,
       not_5_out, not_6_out, or_1_out, or_2_out, or_3_out, or_4_out, xor_1_out;

  assign and_1_out = A & B;  // AND_Gate and_1, 4 bits wide
  assign xor_1_out = A ^ B;  // XOR_Gate xor_1, 4 bits wide
  assign not_1_out = ~A;  // NOT_Gate not_1, 4 bits wide
  assign or_1_out = A | B;  // OR_Gate or_1, 4 bits wide
  assign not_2_out = ~and_1_out;  // NOT_Gate not_2, 4 bits wide
  assign not_3_out = ~B;  // NOT_Gate not_3, 4 bits wide
  assign not_4_out = ~or_1_out;  // NOT_Gate not_4, 4 bits wide
  assign and_2_out = not_1_out & B;  // AND_Gate and_2, 4 bits wide
  assign and_3_out = not_3_out & A;  // AND_Gate and_3, 4 bits wide
  assign or_2_out = not_1_out | B;  // OR_Gate or_2, 4 bits wide
  assign not_5_out = ~xor_1_out;  // NOT_Gate not_5, 4 bits wide
  assign not_6_out = ~A;  // NOT_Gate not_6, 4 bits wide
  assign and_4_out = B & A;  // AND_Gate and_4, 4 bits wide
  assign or_3_out = not_6_out | B;  // OR_Gate or_3, 4 bits wide
  assign or_4_out = B | A;  // OR_Gate or_4, 4 bits wide
  Multiplexer #(.select(4), .width(4), .enable("false")) multiplexer_1 (
    .in0(not_1_out), .in1(not_4_out), .in2(and_2_out), .in3(4'b0000), .in4(not_2_out), .in5(not_3_out),
    .in6(xor_1_out), .in7(and_3_out), .in8(or_2_out), .in9(not_5_out), .in10(B), .in11(and_4_out),
    .in12(4'b0001), .in13(or_3_out), .in14(or_4_out), .in15(A), .out(\Saída ), .sel(\Bits_de_seleção ));
endmodule
